# Fritzing sketch ESP 8266 - RF Transmitter (saved by Fritzing 0.9.3b)

parts:
  ANT1 = Antenna
  U3 = NodeMCU V1.0
  U5 = RF 315/433 Transmitter [package=rf-link_tx]

nets:
  N1: ANT1.antenna_lead, U5.ANT
  N2: U3.D2, U5.DATA
  GND: U3.GND, U5.GND
  VIN: U3.Vin, U5.+5V

notes:
  RF Transmitter
  Green - Gnd
  Yellow - D2
  Red - Vin ( 5V )
  Black - Antenna

custom parts:
  NodeMCU V1.0: ESP8266 based NodeMCU
  RF 315/433 Transmitter: 315/433 Mhz RF Transmitter
